// Logisim project cpu.circ as structural Verilog: 1 circuit, main circuit main
module main (
);

  wire clock_1_out, clock_2_out, clock_3_out, clock_4_out, not_1_out;
  wire [7:0] A, B, ctl, imm, memaddr, memdata;
  wire [15:0] adder_1_out, bit_extender_1_out, multiplexer_1_out, PC;

  // Probe on PC
  // Probe on ctl
  // Probe on imm
  Multiplexer #(.width(16)) multiplexer_1 (
    .in0(16'h1), .in1(bit_extender_1_out), .out(multiplexer_1_out), .sel(ctl[0]), .en(1'b1));
  assign bit_extender_1_out = {{8{imm[7]}}, imm};  // Bit_Extender bit_extender_1
  // Probe on memaddr
  // Probe on memdata
  Adder #(.width(16)) adder_1 (.a(PC), .b(multiplexer_1_out), .out(adder_1_out));  // open: cin, cout
  // Probe on A
  // Probe on B
  Register #(.width(16)) u_PC (.D(adder_1_out), .Q(PC), .clk(clock_1_out));  // open: en, clr
  Clock clock_1 (.out(clock_1_out));
  ROM #(.addrWidth(16), .dataWidth(16)) rom_1 (.addr(PC), .data({imm, ctl}), .sel(1'b1));
  Multiplexer #(.select(2), .width(8)) multiplexer_2 (
    .in0(A), .in1(B), .in2(imm), .in3(imm), .out(memaddr), .sel({ctl[3], ctl[4]}), .en(1'b1));
  not not_1 (not_1_out, ctl[2]);
  Clock clock_2 (.out(clock_2_out));
  RAM #(.bus("asynch")) ram_1 (.addr(memaddr), .data(memdata), .sel(1'b1), .ld(not_1_out));  // open: clr
  Register register_1 (.D(memdata), .en(ctl[5]), .Q(A), .clk(clock_3_out));  // open: clr
  Clock clock_3 (.out(clock_3_out));
  Register register_2 (.D(memdata), .en(ctl[6]), .Q(B), .clk(clock_4_out));  // open: clr
  Clock clock_4 (.out(clock_4_out));

  // Other names for the same wires on the sheet: ctl_jmp = ctl[0]; ctrl_memwr = ctl[2]; ctrl_dstra = ctl[5];
  //   ctrl_dstrb = ctl[6]; ctrl_memaddrrb = ctl[4]; ctrl_memaddrimm = ctl[3]

  // Notes on the sheet:
  //   contents of rom_1 (hex, n*v repeats v):
  //   301 0 0 1
endmodule
